// Logisim project lab3.circ as structural Verilog: 1 circuit, main circuit main
module main (
  input  a,
  input  b
);

  wire and_1_out, and_2_out, and_3_out, and_4_out, and_5_out, and_6_out, and_7_out, and_8_out, and_9_out,
       clock_1_out, not_1_out, not_2_out, not_3_out, not_4_out, or_1_out, or_2_out;
  wire [1:0] register_1_q, undriven;

  Clock clock_1 (.out(clock_1_out));
  not not_1 (not_1_out, undriven[0]);
  not not_2 (not_2_out, undriven[1]);
  Register #(.width(2)) register_1 (.D(undriven), .en(1'b1), .Q(register_1_q), .clk(clock_1_out));  // open: clr
  not not_3 (not_3_out, a);
  not not_4 (not_4_out, b);
  and and_1 (and_1_out, a, undriven[0], not_2_out);
  and and_2 (and_2_out, not_3_out, not_1_out, undriven[1]);
  and and_3 (and_3_out, b, undriven[1]);
  and and_4 (and_4_out, a, not_1_out);
  and and_5 (and_5_out, not_1_out, not_3_out);
  and and_6 (and_6_out, and_3_out, or_1_out);
  or or_1 (or_1_out, and_4_out, undriven[0]);
  and and_7 (and_7_out, a, not_4_out, not_2_out);
  and and_8 (and_8_out, b, undriven[1]);
  and and_9 (and_9_out, and_8_out, or_2_out);
  or or_2 (or_2_out, and_5_out, undriven[0]);
  or or_3 (register_1_q[1], and_1_out, and_2_out, and_6_out);
  or or_4 (register_1_q[0], and_7_out, and_9_out);
  LED led_1 (.in(undriven[1]));

  // Notes on the sheet:
  //   a`
  //   b`
  //   N1
  //   N0
  //   x
endmodule
