// Logisim project lab4.circ as structural Verilog: 1 circuit, main circuit main
module main (
  input  req,
  input  p3s,
  input  p7s,
  input  p37s
);

  wire and_1_out, and_2_out, and_3_out, and_4_out, and_5_out, and_6_out, and_7_out, and_8_out, and_9_out,
       clock_1_out, not_1_out, not_2_out, not_3_out, not_4_out, or_2_out, or_4_out;
  wire [1:0] or_1_out, register_1_q;

  not not_1 (not_1_out, register_1_q[1]);
  Clock clock_1 (.out(clock_1_out));
  not not_2 (not_2_out, p7s);
  and and_1 (and_1_out, req, not_4_out);
  and and_2 (and_2_out, not_1_out, p3s, register_1_q[0]);
  and and_3 (and_3_out, not_4_out, not_3_out);
  not not_3 (not_3_out, p37s);
  not not_4 (not_4_out, register_1_q[0]);
  Register #(.width(2)) register_1 (.D(or_1_out), .en(1'b1), .Q(register_1_q), .clk(clock_1_out));  // open: clr
  and and_4 (and_4_out, register_1_q[1], register_1_q[0], not_2_out);
  or or_1 (or_1_out[0], and_4_out, and_5_out);
  or or_2 (or_2_out, and_1_out, register_1_q[0]);
  and and_5 (and_5_out, or_2_out, not_1_out);
  or or_3 (or_1_out[1], and_2_out, and_6_out);
  or or_4 (or_4_out, and_3_out, register_1_q[0]);
  and and_6 (and_6_out, or_4_out, register_1_q[1]);
  and and_7 (and_7_out, register_1_q[1], register_1_q[0]);
  and and_8 (and_8_out, register_1_q[1], not_4_out);
  and and_9 (and_9_out, not_1_out, not_4_out);
  LED redL (.in(not_1_out));
  LED orrangeL (.in(and_7_out));
  LED greenL (.in(and_8_out));
  LED resetT (.in(and_9_out));

  // Notes on the sheet:
  //   S0
  //   S1
  //   N0
  //   N1
endmodule
