// Logisim project Controller.circ as structural Verilog: 1 circuit, main circuit main
module main (
  input  req,
  input  p3s,
  input  p7s,
  input  p37s,
  input  CLK,
  output redL,
  output orrangeL,
  output greenL,
  output resetT
);

  wire and_1_out, and_2_out, and_3_out, and_4_out, and_5_out, and_6_out, not_2_out, not_3_out, not_4_out,
       or_2_out, or_4_out;
  wire [1:0] or_1_out, register_1_q;

  not not_1 (redL, register_1_q[1]);
  not not_2 (not_2_out, p7s);
  and and_1 (and_1_out, req, not_4_out);
  and and_2 (and_2_out, redL, p3s, register_1_q[0]);
  and and_3 (and_3_out, not_4_out, not_3_out);
  not not_3 (not_3_out, p37s);
  not not_4 (not_4_out, register_1_q[0]);
  Register #(.width(2)) register_1 (.D(or_1_out), .en(1'b1), .Q(register_1_q), .clk(CLK));  // open: clr
  and and_4 (and_4_out, register_1_q[1], register_1_q[0], not_2_out);
  or or_1 (or_1_out[0], and_4_out, and_5_out);
  or or_2 (or_2_out, and_1_out, register_1_q[0]);
  and and_5 (and_5_out, or_2_out, redL);
  or or_3 (or_1_out[1], and_2_out, and_6_out);
  or or_4 (or_4_out, and_3_out, register_1_q[0]);
  and and_6 (and_6_out, or_4_out, register_1_q[1]);
  and and_7 (orrangeL, register_1_q[1], register_1_q[0]);
  and and_8 (greenL, register_1_q[1], not_4_out);
  and and_9 (resetT, redL, not_4_out);

  // Notes on the sheet:
  //   S0
  //   S1
  //   N0
  //   N1
endmodule
