// Logisim project Datapath.circ as structural Verilog: 1 circuit, main circuit main
module main (
  input  counterE,
  input  CLK,
  input  resetT,
  output p3s,
  output p7s,
  output p37s
);

  wire [5:0] counter_1_q;

  Counter #(.width(6), .max('h3f)) counter_1 (
    .count(counterE), .Q(counter_1_q), .clk(CLK), .clr(resetT));  // open: load, D, carry
  Comparator #(.width(6)) comparator_1 (.a(counter_1_q), .b(6'b000011), .eq(p3s));  // open: gt, lt
  Comparator #(.width(6)) comparator_2 (.a(counter_1_q), .b(6'b000111), .eq(p7s));  // open: gt, lt
  Comparator #(.width(6)) comparator_3 (.a(counter_1_q), .b(6'b100101), .eq(p37s));  // open: gt, lt
endmodule
