// Logisim project Main.circ as structural Verilog: 1 circuit, main circuit main
module main (
  input  in_1
);

  wire clock_1_out, main_1_p3s, main_1_p7s, main_1_p37s, main_2_greenl, main_2_orrangel, main_2_redl,
       main_2_resett;

  Datapath_main main_1 (
    .counterE(1'b1), .CLK(clock_1_out), .resetT(main_2_resett), .p3s(main_1_p3s), .p7s(main_1_p7s),
    .p37s(main_1_p37s));
  Clock clock_1 (.out(clock_1_out));
  Controller_main main_2 (
    .req(in_1), .p3s(main_1_p3s), .p7s(main_1_p7s), .p37s(main_1_p37s), .CLK(clock_1_out),
    .redL(main_2_redl), .orrangeL(main_2_orrangel), .greenL(main_2_greenl), .resetT(main_2_resett));
  LED redK (.in(main_2_redl));
  LED orrangeL (.in(main_2_orrangel));
  LED greenL (.in(main_2_greenl));
  LED resetT (.in(main_2_resett));
endmodule
