// Logisim project Controller.circ as structural Verilog: 1 circuit, main circuit main
module main (
  input  diffG,
  input  go,
  input  CLK,
  output x_c,
  output y_c,
  output z_c,
  output diff_c,
  output diff2_c,
  output mux2s,
  output mux1s
);

  wire and_1_out, and_2_out, and_3_out, and_4_out, and_5_out, and_6_out, and_7_out, and_8_out, not_1_out,
       not_2_out, not_3_out, not_4_out, or_1_out, or_4_out, xor_1_out, xor_2_out;
  wire [2:0] or_3_out, register_1_q;

  not not_1 (not_1_out, diffG);
  not not_2 (not_2_out, register_1_q[2]);
  not not_3 (not_3_out, register_1_q[0]);
  not not_4 (not_4_out, register_1_q[1]);
  Register #(.width(3)) register_1 (.D(or_3_out), .en(1'b1), .Q(register_1_q), .clk(CLK));  // open: clr
  and and_1 (and_1_out, not_3_out, register_1_q[1]);
  and and_2 (and_2_out, register_1_q[0], register_1_q[2]);
  and and_3 (and_3_out, and_2_out, or_1_out);
  and and_4 (and_4_out, not_1_out, not_4_out);
  or or_1 (or_1_out, and_4_out, register_1_q[1]);
  and and_5 (and_5_out, not_2_out, register_1_q[0]);
  or or_2 (or_3_out[1], and_5_out, and_6_out);
  and and_6 (and_6_out, register_1_q[1], not_3_out);
  or or_3 (or_3_out[0], go, or_4_out);
  and and_7 (and_7_out, not_2_out, not_4_out, register_1_q[0]);
  or or_4 (or_4_out, and_7_out, and_8_out);
  and and_8 (and_8_out, register_1_q[2], register_1_q[1]);
  and and_9 (x_c, not_2_out, register_1_q[0]);
  and and_10 (z_c, not_4_out, xor_1_out);
  xor xor_1 (xor_1_out, register_1_q[2], register_1_q[0]);
  and and_11 (diff_c, not_3_out, xor_2_out);
  xor xor_2 (xor_2_out, register_1_q[1], register_1_q[2]);
  and and_12 (diff2_c, register_1_q[2], register_1_q[1], register_1_q[0]);
  and and_13 (mux1s, register_1_q[2], not_4_out, not_3_out);
  or or_5 (or_3_out[2], and_1_out, and_3_out);

  assign mux2s = mux1s;
  assign y_c = x_c;

  // Notes on the sheet:
  //   N1
  //   N0
  //   N2
endmodule
