// Logisim project Datapath.circ as structural Verilog: 1 circuit, main circuit main
module main (
  input  diff2_c,
  input  diff_c,
  input  mux1s,
  input  [7:0] x_in,
  input  x_c,
  input  [7:0] y_in,
  input  y_c,
  input  mux2s,
  input  z_c,
  input  CLK,
  output diffG,
  output [7:0] Result
);

  wire [7:0] adder_1_out, diff_q, multiplexer_1_out, multiplexer_2_out, negator_1_out, X_q, Z_q;

  Multiplexer #(.width(8), .enable("false")) multiplexer_1 (
    .in0(8'h1), .in1(Result), .out(multiplexer_1_out), .sel(mux2s));
  Register diff2 (.D(diff_q), .en(diff2_c), .clk(CLK));  // open: Q, clr
  Register diff (.D(adder_1_out), .en(diff_c), .Q(diff_q), .clk(CLK));  // open: clr
  Register X (.D(x_in), .en(x_c), .Q(X_q), .clk(CLK));  // open: clr
  Register Y (.D(y_in), .en(y_c), .clk(CLK));  // open: Q, clr
  Register Z (.D(multiplexer_1_out), .en(CLK), .Q(Z_q), .clk(CLK));  // open: clr
  Comparator comparator_1 (.a(diff_q), .b({8{1'b1}}), .gt(diffG));  // open: eq, lt
  Multiplexer #(.width(8), .enable("false")) multiplexer_2 (
    .in0(X_q), .in1(8'h1), .out(multiplexer_2_out), .sel(mux1s));
  Multiplier multiplier_1 (.a(Z_q), .b(diff_q), .out(Result));  // open: cin, cout
  Negator negator_1 (.in(multiplexer_2_out), .out(negator_1_out));
  Adder adder_1 (.a(diff_q), .b(negator_1_out), .out(adder_1_out));  // open: cin, cout

  assign z_c = CLK;
endmodule
