// Logisim project Main.circ as structural Verilog: 1 circuit, main circuit main
module main (
  input  [7:0] X,
  input  [7:0] Y,
  input  in_3,
  output [7:0] out_4
);

  wire clock_1_out, main_1_diff2_c, main_1_diff_c, main_1_mux1s, main_1_mux2s, main_1_x_c, main_1_y_c,
       main_1_z_c, main_2_diffg;

  Controller_main main_1 (
    .diffG(main_2_diffg), .go(in_3), .CLK(clock_1_out), .x_c(main_1_x_c), .y_c(main_1_y_c), .z_c(main_1_z_c),
    .diff_c(main_1_diff_c), .diff2_c(main_1_diff2_c), .mux2s(main_1_mux2s), .mux1s(main_1_mux1s));
  Clock clock_1 (.out(clock_1_out));
  Datapath_main main_2 (
    .diff2_c(main_1_diff2_c), .diff_c(main_1_diff_c), .x_in(X), .x_c(main_1_x_c), .y_in(Y), .y_c(main_1_y_c),
    .mux2s(main_1_mux2s), .z_c(main_1_z_c), .CLK(clock_1_out), .mux1s(main_1_mux1s), .diffG(main_2_diffg),
    .Result(out_4));
endmodule
