// Logisim project 7SegmentModule.circ as structural Verilog: 1 circuit, main circuit main
module main (
  input  [3:0] INPUT,
  output A,
  output B,
  output C,
  output D,
  output E,
  output F,
  output G,
  output Overflow
);

  _7SegmentDisplay_main main_1 (
    .A(INPUT[3]), .B(INPUT[2]), .C(INPUT[1]), .D(INPUT[0]), .DA(A), .DB(B), .DC(C), .DD(D), .DE(E), .DF(F),
    .DG(G), .Error(Overflow));
endmodule
