// Logisim project InputModule.circ as structural Verilog: 1 circuit, main circuit main
module main (
  input  shiftEnabled,
  input  [7:0] \input ,
  input  Clear,
  input  CLK,
  output [7:0] o7,
  output [7:0] o6,
  output [7:0] o5,
  output [7:0] o4,
  output [7:0] o3,
  output [7:0] o2,
  output [7:0] o1,
  output [7:0] o0
);

  wire [7:0] multiplexer_1_out, multiplexer_2_out, multiplexer_3_out, multiplexer_4_out, multiplexer_5_out,
       multiplexer_6_out, multiplexer_7_out, multiplexer_8_out;

  Multiplexer #(.width(8), .enable("false")) multiplexer_1 (
    .in0(o7), .in1(o6), .out(multiplexer_1_out), .sel(shiftEnabled));
  Register char7 (.D(multiplexer_1_out), .en(1'b1), .Q(o7), .clk(CLK), .clr(Clear));
  Multiplexer #(.width(8), .enable("false")) multiplexer_2 (
    .in0(o6), .in1(o5), .out(multiplexer_2_out), .sel(shiftEnabled));
  Register char6 (.D(multiplexer_2_out), .en(1'b1), .Q(o6), .clk(CLK), .clr(Clear));
  Multiplexer #(.width(8), .enable("false")) multiplexer_3 (
    .in0(o5), .in1(o4), .out(multiplexer_3_out), .sel(shiftEnabled));
  Register char5 (.D(multiplexer_3_out), .en(1'b1), .Q(o5), .clk(CLK), .clr(Clear));
  Multiplexer #(.width(8), .enable("false")) multiplexer_4 (
    .in0(o4), .in1(o3), .out(multiplexer_4_out), .sel(shiftEnabled));
  Register char4 (.D(multiplexer_4_out), .en(1'b1), .Q(o4), .clk(CLK), .clr(Clear));
  Multiplexer #(.width(8), .enable("false")) multiplexer_5 (
    .in0(o3), .in1(o2), .out(multiplexer_5_out), .sel(shiftEnabled));
  Register char3 (.D(multiplexer_5_out), .en(1'b1), .Q(o3), .clk(CLK), .clr(Clear));
  Multiplexer #(.width(8), .enable("false")) multiplexer_6 (
    .in0(o2), .in1(o1), .out(multiplexer_6_out), .sel(shiftEnabled));
  Register char2 (.D(multiplexer_6_out), .en(1'b1), .Q(o2), .clk(CLK), .clr(Clear));
  Multiplexer #(.width(8), .enable("false")) multiplexer_7 (
    .in0(o1), .in1(o0), .out(multiplexer_7_out), .sel(shiftEnabled));
  Register char1 (.D(multiplexer_7_out), .en(1'b1), .Q(o1), .clk(CLK), .clr(Clear));
  Multiplexer #(.width(8), .enable("false")) multiplexer_8 (
    .in0(o0), .in1(\input ), .out(multiplexer_8_out), .sel(shiftEnabled));
  Register char0 (.D(multiplexer_8_out), .en(1'b1), .Q(o0), .clk(CLK), .clr(Clear));
endmodule
