// Logisim project KeyboardModule.circ as structural Verilog: 1 circuit, main circuit main
module main (
  input  A,
  input  B,
  input  C,
  input  D,
  input  E,
  input  F,
  input  G,
  input  H,
  input  I,
  input  J,
  input  K,
  input  L,
  input  M,
  input  N,
  input  O,
  input  P,
  input  Q,
  input  R,
  input  S,
  input  T,
  input  U,
  input  V,
  input  W,
  input  X,
  input  Y,
  input  Z,
  output [4:0] Select
);

  wire nor_1_out, or_1_out, or_5_out, or_7_out;

  nor nor_1 (nor_1_out, A, B, C, D, E, F, G, H, I, J, K, L, M, N, O, P, Q, R, S, T, U, V, W, X, Y, Z);
  or or_1 (or_1_out, C, D, G, H, K, L, O, P, S, T, W, X);
  or or_2 (Select[1], or_1_out, nor_1_out);
  or or_3 (Select[0], Z, X, V, T, R, P, N, L, J, H, F, D, B);
  or or_4 (Select[2], X, W, V, U, P, O, N, M, E, F, G, H);
  or or_5 (or_5_out, I, J, K, L, M, N, O, P, Y, Z);
  or or_6 (Select[3], or_5_out, nor_1_out);
  or or_7 (or_7_out, Q, R, S, T, U, V, W, X, Y, Z);
  or or_8 (Select[4], or_7_out, nor_1_out);

  // Notes on the sheet:
  //   N1
  //   N0
  //   N2
  //   N3
  //   N4
endmodule
