// Logisim project Main.circ as structural Verilog: 1 circuit, main circuit main
module main (
  input  [3:0] Number,
  output Overflow,
  output [7:0] W0,
  output [7:0] W1,
  output [7:0] W2,
  output [7:0] W3,
  output [7:0] W4,
  output [7:0] W5,
  output [7:0] W6,
  output [7:0] W7
);

  wire button_syncronizer_1_p1, button_syncronizer_2_p1, button_syncronizer_3_p1, button_syncronizer_4_p1,
       button_syncronizer_5_p1, button_syncronizer_6_p1, button_syncronizer_7_p1, button_syncronizer_8_p1,
       button_syncronizer_9_p1, button_syncronizer_10_p1, button_syncronizer_11_p1, button_syncronizer_12_p1,
       button_syncronizer_13_p1, button_syncronizer_14_p1, button_syncronizer_15_p1,
       button_syncronizer_16_p1, button_syncronizer_17_p1, button_syncronizer_18_p1,
       button_syncronizer_20_p1, button_syncronizer_21_p1, button_syncronizer_22_p1,
       button_syncronizer_23_p1, button_syncronizer_24_p1, button_syncronizer_25_p2,
       button_syncronizer_26_p1, button_syncronizer_27_p1, clock_1_out, comparator_1_eq, main_3_clr,
       main_3_enable, main_4_a, main_4_b, main_4_c, main_4_d, main_4_e, main_4_f, main_4_g, not_1_out,
       Reset_out;
  wire [4:0] main_1_select;
  wire [6:0] main_3_letter;
  wire [7:0] multiplexer_1_out;

  Clock clock_1 (.out(clock_1_out));
  Button A ();  // open: out
  Button B ();  // open: out
  // Button_Syncronizer button_syncronizer_1: pin names not known; wires that end beside it: button_syncronizer_1_p1
  // Button_Syncronizer button_syncronizer_2: pin names not known; wires that end beside it: button_syncronizer_2_p1
  KeyboardModule_main main_1 (
    .A(button_syncronizer_1_p1), .B(button_syncronizer_2_p1), .C(button_syncronizer_3_p1),
    .D(button_syncronizer_4_p1), .E(button_syncronizer_5_p1), .F(button_syncronizer_6_p1),
    .G(button_syncronizer_8_p1), .H(button_syncronizer_10_p1), .I(button_syncronizer_9_p1),
    .J(button_syncronizer_7_p1), .K(button_syncronizer_14_p1), .L(button_syncronizer_12_p1),
    .M(button_syncronizer_13_p1), .N(button_syncronizer_11_p1), .O(button_syncronizer_17_p1),
    .P(button_syncronizer_15_p1), .Q(button_syncronizer_18_p1), .R(button_syncronizer_16_p1),
    .S(button_syncronizer_22_p1), .T(button_syncronizer_21_p1), .U(button_syncronizer_23_p1),
    .V(button_syncronizer_20_p1), .W(button_syncronizer_27_p1), .X(button_syncronizer_24_p1),
    .Y(button_syncronizer_25_p2), .Z(button_syncronizer_26_p1), .Select(main_1_select));
  Multiplexer #(.select(5), .width(8), .enable("false")) multiplexer_1 (
    .in0(8'h41), .in1(8'h42), .in2(8'h43), .in3(8'h44), .in4(8'h45), .in5(8'h46), .in6(8'h47), .in7(8'h48),
    .in8(8'h49), .in9(8'h4a), .in10(8'h4b), .in11(8'h4c), .in12(8'h4d), .in13(8'h4e), .in14(8'h4f),
    .in15(8'h50), .in16(8'h51), .in17(8'h52), .in18(8'h53), .in19(8'h54), .in20(8'h55), .in21(8'h56),
    .in22(8'h57), .in23(8'h58), .in24(8'h59), .in25(8'h5a), .in26({8{1'b0}}), .out(multiplexer_1_out),
    .sel(main_1_select));  // open: in27, in28, in29, in30, in31
  Button E ();  // open: out
  Button C ();  // open: out
  Button F ();  // open: out
  Button D ();  // open: out
  // Button_Syncronizer button_syncronizer_3: pin names not known; wires that end beside it: button_syncronizer_3_p1
  // Button_Syncronizer button_syncronizer_4: pin names not known; wires that end beside it: button_syncronizer_4_p1
  // Button_Syncronizer button_syncronizer_5: pin names not known; wires that end beside it: button_syncronizer_5_p1
  // Button_Syncronizer button_syncronizer_6: pin names not known; wires that end beside it: button_syncronizer_6_p1
  InputModule_main main_2 (
    .shiftEnabled(not_1_out), .Clear(Reset_out), .CLK(clock_1_out), .\input (multiplexer_1_out), .o7(W0),
    .o6(W1), .o5(W2), .o4(W3), .o3(W4), .o2(W5), .o1(W6), .o0(W7));
  Comparator #(.mode("unsigned")) comparator_1 (
    .a(multiplexer_1_out), .b({8{1'b0}}), .eq(comparator_1_eq));  // open: gt, lt
  not not_1 (not_1_out, comparator_1_eq);
  Button I ();  // open: out
  Button H ();  // open: out
  Button G ();  // open: out
  Button J ();  // open: out
  // Button_Syncronizer button_syncronizer_7: pin names not known; wires that end beside it: button_syncronizer_7_p1
  // Button_Syncronizer button_syncronizer_8: pin names not known; wires that end beside it: button_syncronizer_8_p1
  // Button_Syncronizer button_syncronizer_9: pin names not known; wires that end beside it: button_syncronizer_9_p1
  // Button_Syncronizer button_syncronizer_10: pin names not known; wires that end beside it: button_syncronizer_10_p1
  Button Reset (.out(Reset_out));
  Button L ();  // open: out
  Button N ();  // open: out
  Button K ();  // open: out
  Button M ();  // open: out
  // Button_Syncronizer button_syncronizer_11: pin names not known; wires that end beside it: button_syncronizer_11_p1
  // Button_Syncronizer button_syncronizer_12: pin names not known; wires that end beside it: button_syncronizer_12_p1
  // Button_Syncronizer button_syncronizer_13: pin names not known; wires that end beside it: button_syncronizer_13_p1
  // Button_Syncronizer button_syncronizer_14: pin names not known; wires that end beside it: button_syncronizer_14_p1
  Button P ();  // open: out
  Button O ();  // open: out
  Button Q ();  // open: out
  Button R ();  // open: out
  // Button_Syncronizer button_syncronizer_15: pin names not known; wires that end beside it: button_syncronizer_15_p1
  // Button_Syncronizer button_syncronizer_16: pin names not known; wires that end beside it: button_syncronizer_16_p1
  // Button_Syncronizer button_syncronizer_17: pin names not known; wires that end beside it: button_syncronizer_17_p1
  // Button_Syncronizer button_syncronizer_18: pin names not known; wires that end beside it: button_syncronizer_18_p1
  Button Start ();  // open: out
  // Button_Syncronizer button_syncronizer_19: pin names not known; wires that end beside it: clock_1_out
  Button go ();  // open: out
  Button S ();  // open: out
  Button T ();  // open: out
  Button U ();  // open: out
  Button V ();  // open: out
  // Button_Syncronizer button_syncronizer_20: pin names not known; wires that end beside it: button_syncronizer_20_p1
  // Button_Syncronizer button_syncronizer_21: pin names not known; wires that end beside it: button_syncronizer_21_p1
  // Button_Syncronizer button_syncronizer_22: pin names not known; wires that end beside it: button_syncronizer_22_p1
  // Button_Syncronizer button_syncronizer_23: pin names not known; wires that end beside it: button_syncronizer_23_p1
  TTY tty_1 (.data(main_3_letter), .clk(clock_1_out), .we(main_3_enable), .clr(main_3_clr));
  printModule_main main_3 (
    .MostBs({W3, W2, W1, W0}), .LeastBs({W7, W6, W5, W4}), .clck(clock_1_out), .clr(main_3_clr),
    .Letter(main_3_letter), .Enable(main_3_enable));  // open: go
  Button X ();  // open: out
  Button W ();  // open: out
  Button Z ();  // open: out
  Button Y ();  // open: out
  // Button_Syncronizer button_syncronizer_24: pin names not known; wires that end beside it: button_syncronizer_24_p1
  // Button_Syncronizer button_syncronizer_25: pin names not known; wires that end beside it: clock_1_out, button_syncronizer_25_p2
  // Button_Syncronizer button_syncronizer_26: pin names not known; wires that end beside it: button_syncronizer_26_p1
  // Button_Syncronizer button_syncronizer_27: pin names not known; wires that end beside it: button_syncronizer_27_p1
  _7SegmentModule_main main_4 (
    .INPUT(Number), .A(main_4_a), .B(main_4_b), .C(main_4_c), .D(main_4_d), .E(main_4_e), .F(main_4_f),
    .G(main_4_g), .Overflow(Overflow));
  _7_Segment_Display u_7_segment_display_1 (
    .g(main_4_a), .f(main_4_b), .a(main_4_c), .b(main_4_d), .e(main_4_g), .d(main_4_f), .c(main_4_e));  // open: dp
endmodule
