// Logisim project findNumOfCharsCU.circ as structural Verilog: 1 circuit, main circuit main
module main (
  input  go,
  input  iLd,
  input  lEq,
  input  CLK,
  output incL,
  output incNum,
  output resI,
  output resNum
);

  wire and_2_out, and_3_out, and_4_out, and_5_out, and_6_out, and_7_out, and_9_out, and_10_out, not_1_out,
       not_2_out, not_3_out, not_4_out, or_1_out, or_2_out, or_3_out, xor_1_out;
  wire [2:0] or_4_out, State_q;

  Register #(.width(3)) State (.D(or_4_out), .en(1'b1), .Q(State_q), .clk(CLK));  // open: clr
  not not_1 (not_1_out, State_q[2]);
  not not_2 (not_2_out, State_q[1]);
  not not_3 (not_3_out, State_q[0]);
  and and_1 (or_4_out[2], not_2_out, State_q[0]);
  and and_2 (and_2_out, State_q[2], not_2_out);
  and and_3 (and_3_out, go, not_2_out);
  or or_1 (or_1_out, and_3_out, State_q[1]);
  and and_4 (and_4_out, or_1_out, not_1_out);
  and and_5 (and_5_out, not_1_out, State_q[0]);
  and and_6 (and_6_out, iLd, State_q[1]);
  and and_7 (and_7_out, not_2_out, not_4_out);
  not not_4 (not_4_out, lEq);
  or or_2 (or_2_out, and_2_out, and_4_out);
  and and_8 (or_4_out[1], or_2_out, not_3_out);
  xor xor_1 (xor_1_out, State_q[2], State_q[1]);
  and and_9 (and_9_out, xor_1_out, not_3_out);
  and and_10 (and_10_out, and_5_out, or_3_out);
  or or_3 (or_3_out, and_6_out, and_7_out);
  and and_11 (incL, State_q[2], not_2_out, not_3_out);
  and and_12 (incNum, State_q[2], not_2_out, State_q[0]);
  and and_13 (resI, not_1_out, State_q[1], not_3_out);
  or or_4 (or_4_out[0], and_9_out, and_10_out);

  assign resNum = resI;

  // Notes on the sheet:
  //   N2
  //   N1
  //   N0
endmodule
