// Logisim project findNumOfCharsDP.circ as structural Verilog: 1 circuit, main circuit main
module main (
  input  [7:0] L0,
  input  [7:0] L1,
  input  [7:0] L2,
  input  [7:0] L3,
  input  [7:0] L4,
  input  [7:0] L5,
  input  [7:0] L6,
  input  [7:0] L7,
  input  incL,
  input  resI,
  input  [7:0] cmp,
  input  incNum,
  input  CLK,
  input  resNum,
  output iLd,
  output lEq,
  output [3:0] numOfChars
);

  wire [2:0] bit_extender_1_out;
  wire [3:0] i_q;
  wire [7:0] multiplexer_1_out;

  Counter #(.width(4), .max('hf)) i (.count(incL), .Q(i_q), .clk(CLK), .clr(resI));  // open: load, D, carry
  Counter #(.width(4), .max('hf)) numberOfChards (
    .count(incNum), .Q(numOfChars), .clk(CLK), .clr(resNum));  // open: load, D, carry
  Comparator #(.width(4), .mode("unsigned")) comparator_1 (.a(i_q), .b(4'b1000), .lt(iLd));  // open: gt, eq
  Bit_Extender #(.in_width(4), .out_width(3)) bit_extender_1 (.in(i_q), .out(bit_extender_1_out));
  Multiplexer #(.select(3), .width(8), .enable("false")) multiplexer_1 (
    .in0(L0), .in1(L1), .in2(L2), .in3(L3), .in4(L4), .in5(L5), .in6(L6), .in7(L7), .out(multiplexer_1_out),
    .sel(bit_extender_1_out));
  Comparator #(.mode("unsigned")) comparator_2 (.a(multiplexer_1_out), .b(cmp), .eq(lEq));  // open: gt, lt
endmodule
