// Logisim project findNumOfCharsModule.circ as structural Verilog: 1 circuit, main circuit main
module main (
  input  CLK,
  input  [7:0] L7,
  input  [7:0] L6,
  input  go,
  input  [7:0] L5,
  input  [7:0] L4,
  input  [7:0] cmp,
  input  [7:0] L3,
  input  [7:0] L2,
  input  [7:0] L1,
  input  [7:0] L0,
  output [3:0] numOfChars
);

  wire main_1_ild, main_1_leq, main_2_incl, main_2_incnum, main_2_resi, main_2_resnum;

  findNumOfCharsDP_main main_1 (
    .incL(main_2_incl), .cmp(cmp), .incNum(main_2_incnum), .CLK(CLK), .resI(main_2_resi),
    .resNum(main_2_resnum), .L0(L0), .L1(L1), .L2(L2), .L3(L3), .L4(L4), .L5(L5), .L6(L6), .L7(L7),
    .iLd(main_1_ild), .lEq(main_1_leq), .numOfChars(numOfChars));
  findNumOfCharsCU_main main_2 (
    .go(go), .iLd(main_1_ild), .lEq(main_1_leq), .CLK(CLK), .incL(main_2_incl), .incNum(main_2_incnum),
    .resI(main_2_resi), .resNum(main_2_resnum));
endmodule
