// Logisim project findNumOfCharsTest.circ as structural Verilog: 1 circuit, main circuit main
module main (
  input  [7:0] L7,
  input  [7:0] L6,
  input  [7:0] L5,
  input  [7:0] CMP,
  input  [7:0] L4,
  input  [7:0] L3,
  input  [7:0] L2,
  input  [7:0] L1,
  input  [7:0] L0,
  output [3:0] out_10
);

  wire clock_1_out, go_out;

  Clock clock_1 (.out(clock_1_out));
  Button go (.out(go_out));
  findNumOfCharsModule_main main_1 (
    .L7(L7), .L6(L6), .L5(L5), .L4(L4), .L3(L3), .L2(L2), .L1(L1), .L0(L0), .numOfChars(out_10),
    .CLK(clock_1_out), .go(go_out), .cmp(CMP));
endmodule
