// Logisim project initializeCU.circ as structural Verilog: 1 circuit, main circuit main
module main (
  input  iLt,
  input  go,
  input  CLK,
  output incL,
  output resL
);

  wire and_1_out, and_2_out, and_3_out, and_5_out, and_6_out, and_7_out, and_9_out, not_1_out, not_2_out,
       not_3_out, or_1_out, or_2_out;
  wire [2:0] and_4_out, register_1_q;

  and and_1 (and_1_out, not_3_out, register_1_q[1], not_2_out);
  and and_2 (and_2_out, register_1_q[1], not_2_out, iLt);
  and and_3 (and_3_out, not_1_out, go);
  and and_4 (and_4_out[0], register_1_q[2], not_1_out, not_2_out);
  not not_1 (not_1_out, register_1_q[1]);
  not not_2 (not_2_out, register_1_q[0]);
  not not_3 (not_3_out, register_1_q[2]);
  Register #(.width(3)) register_1 (.D(and_4_out), .Q(register_1_q), .clk(CLK));  // open: en, clr
  or or_1 (or_1_out, and_2_out, not_1_out);
  and and_5 (and_5_out, or_1_out, register_1_q[2]);
  or or_2 (or_2_out, and_3_out, register_1_q[1]);
  and and_6 (and_6_out, or_2_out, not_3_out, not_2_out);
  and and_7 (and_7_out, register_1_q[2], not_1_out, register_1_q[0]);
  and and_8 (resL, not_3_out, register_1_q[1], not_2_out);
  or or_3 (incL, resL, and_9_out);
  and and_9 (and_9_out, register_1_q[2], not_1_out, register_1_q[0]);
  or or_4 (and_4_out[2], and_1_out, and_5_out);
  or or_5 (and_4_out[1], and_6_out, and_7_out);

  // Notes on the sheet:
  //   N2
  //   N1
  //   N0
endmodule
