// Logisim project initializeDP.circ as structural Verilog: 1 circuit, main circuit main
module main (
  input  [3:0] numOfChars,
  input  incL,
  input  resL,
  input  CLK,
  output iLt,
  output [7:0] T0,
  output [7:0] T1,
  output [7:0] T2,
  output [7:0] T3,
  output [7:0] T4,
  output [7:0] T5,
  output [7:0] T6,
  output [7:0] T7
);

  wire main_1_l0, main_1_l1, main_1_l2, main_1_l3, main_1_l4, main_1_l5, main_1_l6, main_1_l7;
  wire [2:0] bit_extender_1_out;
  wire [3:0] counter_1_q;

  Counter #(.width(4), .max('hf)) counter_1 (
    .count(incL), .Q(counter_1_q), .clk(CLK), .clr(resL));  // open: load, D, carry
  Comparator #(.width(4), .mode("unsigned")) comparator_1 (.a(counter_1_q), .b(numOfChars), .lt(iLt));  // open: gt, eq
  Bit_Extender #(.in_width(4), .out_width(3)) bit_extender_1 (.in(counter_1_q), .out(bit_extender_1_out));
  wordSplitter_main main_1 (
    .S2(bit_extender_1_out[2]), .S1(bit_extender_1_out[1]), .S0(bit_extender_1_out[0]), .l0(main_1_l0),
    .l1(main_1_l1), .l2(main_1_l2), .l3(main_1_l3), .l4(main_1_l4), .l5(main_1_l5), .l6(main_1_l6),
    .l7(main_1_l7));
  Register register_1 (.D(8'h5f), .en(main_1_l0), .Q(T0), .clk(CLK));  // open: clr
  Register register_2 (.D(8'h5f), .en(main_1_l1), .Q(T1), .clk(CLK));  // open: clr
  Register register_3 (.D(8'h5f), .en(main_1_l2), .Q(T2), .clk(CLK));  // open: clr
  Register register_4 (.D(8'h5f), .en(main_1_l3), .Q(T3), .clk(CLK));  // open: clr
  Register register_5 (.D(8'h5f), .en(main_1_l4), .Q(T4), .clk(CLK));  // open: clr
  Register register_6 (.D(8'h5f), .en(main_1_l5), .Q(T5), .clk(CLK));  // open: clr
  Register register_7 (.D(8'h5f), .en(main_1_l6), .Q(T6), .clk(CLK));  // open: clr
  Register register_8 (.D(8'h5f), .en(main_1_l7), .Q(T7), .clk(CLK));  // open: clr
endmodule
