// Logisim project initializeModule.circ as structural Verilog: 1 circuit, main circuit main
module main (
  input  [3:0] numOfChars,
  input  go,
  input  CLK,
  output [7:0] T0,
  output [7:0] T1,
  output [7:0] T2,
  output [7:0] T3,
  output [7:0] T4,
  output [7:0] T5,
  output [7:0] T6,
  output [7:0] T7
);

  wire main_1_ilt, main_2_incl, main_2_resl;

  initializeDP_main main_1 (
    .numOfChars(numOfChars), .incL(main_2_incl), .CLK(CLK), .resL(main_2_resl), .iLt(main_1_ilt), .T0(T0),
    .T1(T1), .T2(T2), .T3(T3), .T4(T4), .T5(T5), .T6(T6), .T7(T7));
  initializeCU_main main_2 (.iLt(main_1_ilt), .go(go), .CLK(CLK), .incL(main_2_incl), .resL(main_2_resl));
endmodule
