// Logisim project initializeTest.circ as structural Verilog: 1 circuit, main circuit main
module main (
  input  [3:0] numOfChars,
  output [7:0] T0,
  output [7:0] T1,
  output [7:0] T2,
  output [7:0] T3,
  output [7:0] T4,
  output [7:0] T5,
  output [7:0] T6,
  output [7:0] T7
);

  wire button_1_out, clock_1_out;

  Button button_1 (.out(button_1_out));
  Clock clock_1 (.out(clock_1_out));
  initializeModule_main main_1 (
    .numOfChars(numOfChars), .go(button_1_out), .CLK(clock_1_out), .T0(T0), .T1(T1), .T2(T2), .T3(T3),
    .T4(T4), .T5(T5), .T6(T6), .T7(T7));
endmodule
