// Logisim project mainDP.circ as structural Verilog: 1 circuit, main circuit main
module main (
  input  CLK,
  input  f1Go,
  input  inGo,
  input  [7:0] W0,
  input  f2Go,
  input  [7:0] W1,
  input  [7:0] W2,
  input  [7:0] W3,
  input  [7:0] W4,
  input  [7:0] W5,
  input  [7:0] W6,
  input  [7:0] W7,
  input  iIncL,
  input  matchGo,
  input  iResL,
  input  mIncL,
  input  mResL,
  input  [7:0] pressedLetter,
  output zEq,
  output fEq,
  output iLt,
  output lEq,
  output mEq
);

  wire [2:0] bit_extender_1_out;
  wire [3:0] counter_1_q, main_2_numofchars, main_4_numofchars, missMatch_q, numOfChars_q;
  wire [7:0] main_1_m0, main_1_m1, main_1_m2, main_1_m3, main_1_m4, main_1_m5, main_1_m6, main_1_m7,
       main_3_t0, main_3_t1, main_3_t2, main_3_t3, main_3_t4, main_3_t5, main_3_t6, main_3_t7,
       multiplexer_2_out, multiplexer_3_out, multiplexer_4_out, multiplexer_5_out, multiplexer_6_out,
       multiplexer_7_out, multiplexer_8_out, multiplexer_9_out, multiplexer_10_out, Taken0_q, Taken1_q,
       Taken2_q, Taken3_q, Taken4_q, Taken5_q, Taken6_q, Taken7_q, Typed0_q, Typed1_q, Typed2_q, Typed3_q,
       Typed4_q, Typed5_q, Typed6_q, Typed7_q;

  Comparator #(.mode("unsigned")) comparator_1 (.a({8{1'b0}}), .b(pressedLetter), .eq(lEq));  // open: gt, lt
  matchedGivenLetterModule_main main_1 (
    .M7(main_1_m7), .M6(main_1_m6), .M5(main_1_m5), .M4(main_1_m4), .M3(main_1_m3), .M2(main_1_m2),
    .M1(main_1_m1), .M0(main_1_m0), .W7(W7), .W6(W6), .W5(W5), .W4(W4), .W3(W3), .W2(W2), .W1(W1), .W0(W0),
    .Letter(pressedLetter), .CLK(CLK), .go(matchGo));
  findNumOfCharsModule_main main_2 (
    .L7(W7), .L6(W6), .L5(W5), .L4(W4), .L3(W3), .L2(W2), .L1(W1), .L0(W0), .numOfChars(main_2_numofchars),
    .CLK(CLK), .go(f1Go), .cmp({8{1'b0}}));
  Register #(.width(4)) numOfChars (.D(main_2_numofchars), .Q(numOfChars_q));  // open: en, clk, clr
  initializeModule_main main_3 (
    .numOfChars(numOfChars_q), .go(inGo), .CLK(CLK), .T0(main_3_t0), .T1(main_3_t1), .T2(main_3_t2),
    .T3(main_3_t3), .T4(main_3_t4), .T5(main_3_t5), .T6(main_3_t6), .T7(main_3_t7));
  Register Taken0 (.D(main_1_m0), .Q(Taken0_q));  // open: en, clk, clr
  Multiplexer #(.select(3), .width(8), .enable("false")) multiplexer_1 (
    .in0(Taken0_q), .in1(Taken1_q), .in2(Taken2_q), .in3(Taken3_q), .in4(Taken4_q), .in5(Taken5_q),
    .in6(Taken6_q), .in7(Taken7_q));  // open: out, sel
  Register Taken1 (.D(main_1_m1), .Q(Taken1_q), .clk(CLK));  // open: en, clr
  Register Typed0 (.D(multiplexer_2_out), .Q(Typed0_q), .clk(CLK));  // open: en, clr
  Multiplexer #(.width(8)) multiplexer_2 (.in0(Typed0_q), .in1(main_3_t0), .out(multiplexer_2_out));  // open: sel, en
  Register Typed1 (.D(multiplexer_3_out), .Q(Typed1_q), .clk(CLK));  // open: en, clr
  Multiplexer #(.width(8)) multiplexer_3 (.in0(Typed1_q), .in1(main_3_t1), .out(multiplexer_3_out));  // open: sel, en
  Comparator #(.width(4), .mode("unsigned")) comparator_2 (
    .a(4'b0000), .b(main_4_numofchars), .eq(zEq));  // open: gt, lt
  findNumOfCharsModule_main main_4 (
    .L7(Taken7_q), .L6(Taken6_q), .L5(Taken5_q), .L4(Taken4_q), .L3(Taken3_q), .L2(Taken2_q), .L1(Taken1_q),
    .L0(Taken0_q), .numOfChars(main_4_numofchars), .CLK(CLK), .go(f2Go), .cmp(8'h5f));
  Multiplexer #(.select(3), .width(8), .enable("false")) multiplexer_4 (
    .in0(Taken0_q), .in1(Taken1_q), .in2(Taken2_q), .in3(Taken3_q), .in4(Taken4_q), .in5(Taken5_q),
    .in6(Taken6_q), .in7(Taken7_q), .out(multiplexer_4_out), .sel(bit_extender_1_out));
  Register Taken2 (.D(main_1_m2), .Q(Taken2_q), .clk(CLK));  // open: en, clr
  Register Typed2 (.D(multiplexer_5_out), .Q(Typed2_q), .clk(CLK));  // open: en, clr
  Comparator #(.mode("unsigned")) comparator_3 (.a(multiplexer_4_out), .b({8{1'b0}}), .eq(fEq));  // open: gt, lt
  Register Taken3 (.D(main_1_m3), .Q(Taken3_q), .clk(CLK));  // open: en, clr
  Multiplexer #(.width(8)) multiplexer_5 (.in0(Typed2_q), .in1(main_3_t2), .out(multiplexer_5_out));  // open: sel, en
  Register Taken4 (.D(main_1_m4), .Q(Taken4_q), .clk(CLK));  // open: en, clr
  Register Typed3 (.D(multiplexer_6_out), .Q(Typed3_q), .clk(CLK));  // open: en, clr
  Multiplexer #(.width(8)) multiplexer_6 (.in0(Typed3_q), .in1(main_3_t3), .out(multiplexer_6_out));  // open: sel, en
  Register Taken5 (.D(main_1_m5), .Q(Taken5_q), .clk(CLK));  // open: en, clr
  Register Typed4 (.D(multiplexer_7_out), .Q(Typed4_q), .clk(CLK));  // open: en, clr
  Multiplexer #(.width(8)) multiplexer_7 (.in0(Typed4_q), .in1(main_3_t4), .out(multiplexer_7_out));  // open: sel, en
  Register Typed5 (.D(multiplexer_8_out), .Q(Typed5_q), .clk(CLK));  // open: en, clr
  Multiplexer #(.width(8)) multiplexer_8 (.in0(Typed5_q), .in1(main_3_t5), .out(multiplexer_8_out));  // open: sel, en
  Register Taken6 (.D(main_1_m6), .Q(Taken6_q), .clk(CLK));  // open: en, clr
  Register Typed6 (.D(multiplexer_9_out), .Q(Typed6_q), .clk(CLK));  // open: en, clr
  Register Taken7 (.D(main_1_m7), .Q(Taken7_q), .clk(CLK));  // open: en, clr
  Multiplexer #(.width(8)) multiplexer_9 (.in0(Typed6_q), .in1(main_3_t6), .out(multiplexer_9_out));  // open: sel, en
  Counter #(.width(4), .max('hf)) counter_1 (
    .count(iIncL), .Q(counter_1_q), .clk(CLK), .clr(iResL));  // open: load, D, carry
  Counter #(.width(4), .max('hf)) missMatch (
    .count(mIncL), .Q(missMatch_q), .clk(CLK), .clr(mResL));  // open: load, D, carry
  Register Typed7 (.D(multiplexer_10_out), .Q(Typed7_q), .clk(CLK));  // open: en, clr
  Multiplexer #(.width(8)) multiplexer_10 (.in0(Typed7_q), .in1(main_3_t7), .out(multiplexer_10_out));  // open: sel, en
  Comparator #(.width(4), .mode("unsigned")) comparator_4 (.a(counter_1_q), .b(4'b1000), .lt(iLt));  // open: gt, eq
  Bit_Extender #(.in_width(4), .out_width(3)) bit_extender_1 (.in(counter_1_q), .out(bit_extender_1_out));
  Comparator #(.width(4), .mode("unsigned")) comparator_5 (.a(4'b1010), .b(missMatch_q), .eq(mEq));  // open: gt, lt
endmodule
