// Logisim project matchGivenLetterTest.circ as structural Verilog: 1 circuit, main circuit main
module main (
  input  [7:0] Letter,
  input  [7:0] W7,
  input  [7:0] W6,
  input  [7:0] W5,
  input  [7:0] W4,
  input  [7:0] W3,
  input  [7:0] W2,
  input  [7:0] W1,
  input  [7:0] W0,
  output [7:0] M7,
  output [7:0] M6,
  output [7:0] M5,
  output [7:0] M4,
  output [7:0] M3,
  output [7:0] M2,
  output [7:0] M1,
  output [7:0] M0
);

  wire button_1_out, clock_1_out;

  matchedGivenLetterModule_main main_1 (
    .M7(M7), .M6(M6), .M5(M5), .M4(M4), .M3(M3), .M2(M2), .M1(M1), .M0(M0), .W7(W7), .W6(W6), .W5(W5),
    .W4(W4), .W3(W3), .W2(W2), .W1(W1), .W0(W0), .Letter(Letter), .CLK(clock_1_out), .go(button_1_out));
  Clock clock_1 (.out(clock_1_out));
  Button button_1 (.out(button_1_out));
endmodule
