// Logisim project matchedGivenLetterCU.circ as structural Verilog: 1 circuit, main circuit main
module main (
  input  go,
  input  lEq,
  input  iL,
  input  CLK,
  output li,
  output ri,
  output cL
);

  wire and_1_out, and_2_out, and_4_out, and_5_out, and_6_out, and_7_out, and_8_out, and_9_out, not_1_out,
       not_2_out, not_3_out, not_4_out, or_1_out, or_2_out, or_4_out, or_5_out;
  wire [2:0] and_13_out, register_1_q;

  not not_1 (not_1_out, register_1_q[2]);
  not not_2 (not_2_out, register_1_q[1]);
  not not_3 (not_3_out, register_1_q[0]);
  Register #(.width(3)) register_1 (.D(and_13_out), .en(1'b1), .Q(register_1_q), .clk(CLK));  // open: clr
  and and_1 (and_1_out, not_1_out, iL);
  or or_1 (or_1_out, and_1_out, register_1_q[2]);
  not not_4 (not_4_out, lEq);
  and and_2 (and_2_out, or_1_out, register_1_q[1]);
  or or_2 (or_2_out, and_2_out, and_4_out);
  and and_3 (and_13_out[2], or_2_out, not_3_out);
  and and_4 (and_4_out, register_1_q[2], not_2_out);
  and and_5 (and_5_out, not_2_out, register_1_q[0]);
  or or_3 (and_13_out[1], and_5_out, and_6_out);
  and and_6 (and_6_out, not_1_out, register_1_q[1], not_3_out, iL);
  and and_7 (and_7_out, not_1_out, go);
  or or_4 (or_4_out, and_7_out, register_1_q[2]);
  and and_8 (and_8_out, or_4_out, not_2_out);
  and and_9 (and_9_out, register_1_q[2], register_1_q[1], not_4_out);
  and and_10 (li, not_2_out, register_1_q[0]);
  and and_11 (ri, not_1_out, not_2_out, register_1_q[0]);
  and and_12 (cL, register_1_q[2], not_2_out, not_3_out);
  or or_5 (or_5_out, and_8_out, and_9_out);
  and and_13 (and_13_out[0], or_5_out, not_3_out);

  // Notes on the sheet:
  //   N2
  //   N1
  //   N0
endmodule
