// Logisim project matchedGivenLetterDP.circ as structural Verilog: 1 circuit, main circuit main
module main (
  input  [7:0] W7,
  input  [7:0] W6,
  input  [7:0] W5,
  input  [7:0] W4,
  input  cL,
  input  [7:0] W3,
  input  [7:0] W2,
  input  [7:0] W1,
  input  [7:0] W0,
  input  [7:0] Letter,
  input  li,
  input  ri,
  input  CLK,
  output [7:0] M7,
  output [7:0] M6,
  output [7:0] M5,
  output lEq,
  output iL,
  output [7:0] M4,
  output [7:0] M3,
  output [7:0] M2,
  output [7:0] M1,
  output [7:0] M0
);

  wire and_1_out, and_2_out, and_3_out, and_4_out, and_5_out, and_6_out, and_7_out, and_8_out, main_1_l0,
       main_1_l1, main_1_l2, main_1_l3, main_1_l4, main_1_l5, main_1_l6, main_1_l7;
  wire [2:0] bit_extender_1_out;
  wire [3:0] i_q;
  wire [7:0] multiplexer_1_out;

  Register register_1 (.D(W7), .en(and_1_out), .Q(M7), .clk(CLK));  // open: clr
  Register register_2 (.D(W6), .en(and_2_out), .Q(M6), .clk(CLK));  // open: clr
  Register register_3 (.D(W5), .en(and_3_out), .Q(M5), .clk(CLK));  // open: clr
  Register register_4 (.D(W4), .en(and_4_out), .Q(M4), .clk(CLK));  // open: clr
  Register register_5 (.D(W3), .en(and_5_out), .Q(M3), .clk(CLK));  // open: clr
  Register register_6 (.D(W2), .en(and_6_out), .Q(M2), .clk(CLK));  // open: clr
  Register register_7 (.D(W1), .en(and_7_out), .Q(M1), .clk(CLK));  // open: clr
  Register register_8 (.D(W0), .en(and_8_out), .Q(M0), .clk(CLK));  // open: clr
  and and_1 (and_1_out, cL, main_1_l7);
  and and_2 (and_2_out, cL, main_1_l6);
  and and_3 (and_3_out, cL, main_1_l5);
  and and_4 (and_4_out, cL, main_1_l4);
  and and_5 (and_5_out, cL, main_1_l3);
  and and_6 (and_6_out, cL, main_1_l2);
  and and_7 (and_7_out, cL, main_1_l1);
  and and_8 (and_8_out, cL, main_1_l0);
  wordSplitter_main main_1 (
    .S2(bit_extender_1_out[2]), .S1(bit_extender_1_out[1]), .S0(bit_extender_1_out[0]), .l0(main_1_l0),
    .l1(main_1_l1), .l2(main_1_l2), .l3(main_1_l3), .l4(main_1_l4), .l5(main_1_l5), .l6(main_1_l6),
    .l7(main_1_l7));
  Counter #(.width(4), .max('hf)) i (.count(li), .Q(i_q), .clk(CLK), .clr(ri));  // open: load, D, carry
  Comparator #(.width(4), .mode("unsigned")) comparator_1 (.a(i_q), .b(4'b1000), .lt(iL));  // open: gt, eq
  Bit_Extender #(.in_width(4), .out_width(3)) bit_extender_1 (.in(i_q), .out(bit_extender_1_out));
  Multiplexer #(.select(3), .width(8), .enable("false")) multiplexer_1 (
    .in0(W0), .in1(W1), .in2(W2), .in3(W3), .in4(W4), .in5(W5), .in6(W6), .in7(W7), .out(multiplexer_1_out),
    .sel(bit_extender_1_out));
  Comparator #(.mode("unsigned")) comparator_2 (.a(multiplexer_1_out), .b(Letter), .eq(lEq));  // open: gt, lt
endmodule
