// Logisim project matchedGivenLetterModule.circ as structural Verilog: 1 circuit, main circuit main
module main (
  input  [7:0] Letter,
  input  [7:0] W7,
  input  [7:0] W6,
  input  CLK,
  input  [7:0] W5,
  input  [7:0] W4,
  input  go,
  input  [7:0] W3,
  input  [7:0] W2,
  input  [7:0] W1,
  input  [7:0] W0,
  output [7:0] M7,
  output [7:0] M6,
  output [7:0] M5,
  output [7:0] M4,
  output [7:0] M3,
  output [7:0] M2,
  output [7:0] M1,
  output [7:0] M0
);

  wire main_1_il, main_1_leq, main_2_cl, main_2_li, main_2_ri;

  matchedGivenLetterDP_main main_1 (
    .li(main_2_li), .CLK(CLK), .cL(main_2_cl), .ri(main_2_ri), .Letter(Letter), .W7(W7), .W6(W6), .W5(W5),
    .W4(W4), .M7(M7), .W3(W3), .W2(W2), .W1(W1), .W0(W0), .M6(M6), .M5(M5), .lEq(main_1_leq), .iL(main_1_il),
    .M4(M4), .M3(M3), .M2(M2), .M1(M1), .M0(M0));
  matchedGivenLetterCU_main main_2 (
    .go(go), .lEq(main_1_leq), .iL(main_1_il), .CLK(CLK), .li(main_2_li), .ri(main_2_ri), .cL(main_2_cl));
endmodule
