// Logisim project printCU.circ as structural Verilog: 1 circuit, main circuit main
module main (
  input  go,
  input  clck,
  output clr,
  output m1,
  output m0,
  output Enable,
  output bitsSelect
);

  wire and_1_out, and_2_out, and_3_out, and_4_out, and_5_out, and_6_out, and_7_out, and_8_out, and_9_out,
       and_10_out, and_11_out, and_12_out, not_1_out, not_2_out, not_3_out, not_4_out, not_5_out, not_6_out,
       not_7_out, not_8_out, not_9_out, not_10_out, not_11_out, not_12_out, not_13_out, not_14_out,
       not_15_out, not_16_out, not_17_out, not_18_out, not_19_out, not_20_out, not_21_out, not_22_out,
       not_23_out, not_24_out, not_25_out, not_26_out;
  wire [3:0] or_6_out;
  wire [3:1] register_1_q;

  not not_1 (not_1_out, register_1_q[3]);
  not not_2 (not_2_out, register_1_q[2]);
  not not_3 (not_3_out, register_1_q[1]);
  not not_4 (not_4_out, m0);
  not not_5 (not_5_out, register_1_q[3]);
  not not_6 (not_6_out, register_1_q[2]);
  not not_7 (not_7_out, register_1_q[3]);
  not not_8 (not_8_out, register_1_q[1]);
  not not_9 (not_9_out, register_1_q[3]);
  not not_10 (not_10_out, m0);
  not not_11 (not_11_out, register_1_q[3]);
  not not_12 (not_12_out, register_1_q[1]);
  not not_13 (not_13_out, register_1_q[3]);
  not not_14 (not_14_out, m0);
  not not_15 (not_15_out, register_1_q[3]);
  not not_16 (not_16_out, m0);
  not not_17 (not_17_out, register_1_q[3]);
  not not_18 (not_18_out, m0);
  not not_19 (not_19_out, register_1_q[3]);
  not not_20 (not_20_out, m0);
  not not_21 (not_21_out, register_1_q[2]);
  not not_22 (not_22_out, register_1_q[1]);
  not not_23 (not_23_out, m0);
  not not_24 (not_24_out, register_1_q[3]);
  not not_25 (not_25_out, register_1_q[2]);
  not not_26 (not_26_out, register_1_q[1]);
  not not_27 (m1, register_1_q[1]);
  or or_1 (Enable, register_1_q[1], register_1_q[2], register_1_q[3]);
  and and_1 (and_1_out, register_1_q[2], register_1_q[1]);
  and and_2 (and_2_out, not_1_out, register_1_q[2], register_1_q[1], m0);
  and and_3 (and_3_out, register_1_q[3], not_2_out, not_3_out, not_4_out);
  and and_4 (and_4_out, not_5_out, not_6_out, register_1_q[1], m0);
  and and_5 (and_5_out, not_7_out, register_1_q[2], not_8_out);
  and and_6 (and_6_out, not_9_out, register_1_q[2], not_10_out);
  and and_7 (and_7_out, not_11_out, not_12_out, m0);
  and and_8 (and_8_out, not_13_out, register_1_q[1], not_14_out);
  and and_9 (and_9_out, not_15_out, not_16_out, go);
  and and_10 (and_10_out, not_17_out, register_1_q[1], not_18_out);
  and and_11 (and_11_out, not_19_out, register_1_q[2], not_20_out);
  and and_12 (and_12_out, register_1_q[3], not_21_out, not_22_out, not_23_out);
  and and_13 (clr, not_24_out, not_25_out, not_26_out, m0);
  or or_2 (bitsSelect, and_1_out, register_1_q[3]);
  Register #(.width(4)) register_1 (.D(or_6_out), .en(1'b1), .Q({register_1_q, m0}), .clk(clck));  // open: clr
  or or_3 (or_6_out[3], and_2_out, and_3_out);
  or or_4 (or_6_out[2], and_4_out, and_5_out, and_6_out);
  or or_5 (or_6_out[1], and_7_out, and_8_out);
  or or_6 (or_6_out[0], and_9_out, and_10_out, and_11_out, and_12_out);
endmodule
