// Logisim project printDP.circ as structural Verilog: 1 circuit, main circuit main
module main (
  input  [31:0] MostBs,
  input  bitsSelector,
  input  [31:0] LeastBs,
  input  [1:0] mux,
  output [6:0] Letter
);

  wire [7:0] multiplexer_1_out, multiplexer_2_out, multiplexer_3_out;

  Multiplexer #(.select(2), .width(8), .enable("false")) multiplexer_1 (
    .in0(MostBs[7:0]), .in1(MostBs[15:8]), .in2(MostBs[23:16]), .in3(MostBs[31:24]), .out(multiplexer_1_out),
    .sel(mux));
  Multiplexer #(.select(2), .width(8), .enable("false")) multiplexer_2 (
    .in0(LeastBs[7:0]), .in1(LeastBs[15:8]), .in2(LeastBs[23:16]), .in3(LeastBs[31:24]),
    .out(multiplexer_2_out), .sel(mux));
  Multiplexer #(.width(8), .enable("false")) multiplexer_3 (
    .in0(multiplexer_1_out), .in1(multiplexer_2_out), .out(multiplexer_3_out), .sel(bitsSelector));
  Bit_Extender #(.out_width(7)) bit_extender_1 (.in(multiplexer_3_out), .out(Letter));
endmodule
