// Logisim project printModule.circ as structural Verilog: 1 circuit, main circuit main
module main (
  input  go,
  input  [31:0] MostBs,
  input  clck,
  input  [31:0] LeastBs,
  output clr,
  output [6:0] Letter,
  output Enable
);

  wire main_2_bitsselect;
  wire [1:0] main_2_m0;

  printDP_main main_1 (
    .MostBs(MostBs), .LeastBs(LeastBs), .mux(main_2_m0), .bitsSelector(main_2_bitsselect), .Letter(Letter));
  printCU_main main_2 (
    .go(go), .clck(clck), .clr(clr), .m1(main_2_m0[1]), .m0(main_2_m0[0]), .Enable(Enable),
    .bitsSelect(main_2_bitsselect));
endmodule
