// Logisim project wordSplitter.circ as structural Verilog: 1 circuit, main circuit main
module main (
  input  S2,
  input  S1,
  input  S0,
  output l0,
  output l1,
  output l2,
  output l3,
  output l4,
  output l5,
  output l6,
  output l7
);

  wire not_1_out, not_2_out, not_3_out, not_4_out, not_5_out, not_6_out, not_7_out, not_8_out, not_9_out,
       not_10_out, not_11_out, not_12_out;

  not not_1 (not_1_out, S2);
  not not_2 (not_2_out, S1);
  not not_3 (not_3_out, S0);
  not not_4 (not_4_out, S2);
  not not_5 (not_5_out, S1);
  not not_6 (not_6_out, S2);
  not not_7 (not_7_out, S0);
  not not_8 (not_8_out, S2);
  not not_9 (not_9_out, S1);
  not not_10 (not_10_out, S0);
  not not_11 (not_11_out, S1);
  not not_12 (not_12_out, S0);
  and and_1 (l7, S2, S1, S0);
  and and_2 (l0, not_1_out, not_2_out, not_3_out);
  and and_3 (l1, not_4_out, not_5_out, S0);
  and and_4 (l2, not_6_out, S1, not_7_out);
  and and_5 (l3, not_8_out, S1, S0);
  and and_6 (l4, S2, not_9_out, not_10_out);
  and and_7 (l5, S2, not_11_out, S0);
  and and_8 (l6, S2, S1, not_12_out);
endmodule
