// Logisim project Logisim.circ as structural Verilog: 1 circuit, main circuit main
module main (
);

  wire and_1_out, and_4_out, and_7_out, and_8_out, and_9_out, and_10_out, and_11_out, and_12_out, and_13_out,
       and_14_out, and_15_out, and_16_out, and_17_out, and_18_out, and_19_out, and_20_out, and_21_out,
       and_22_out, and_23_out, and_24_out, and_25_out, and_26_out, and_30_out, and_31_out, button_1_out,
       button_2_out, button_3_out, clock_1_out, not_1_out, not_2_out, not_3_out, not_4_out, not_5_out,
       not_6_out, not_7_out, not_8_out, not_9_out, not_10_out, not_11_out, not_12_out, not_13_out,
       not_14_out, not_15_out, not_16_out, not_17_out, not_18_out, not_19_out, not_20_out, not_21_out,
       not_22_out, not_23_out, not_24_out, not_25_out, not_26_out, not_27_out, not_28_out, not_29_out,
       not_30_out, not_31_out, not_32_out, not_33_out, not_34_out, not_35_out, not_36_out, not_37_out,
       not_38_out, not_39_out, not_40_out, not_41_out, not_42_out, not_43_out, not_44_out, not_45_out,
       not_46_out, not_47_out, not_48_out, not_49_out, or_1_out, or_2_out, or_3_out, or_4_out, or_5_out,
       or_6_out, xnor_1_out, xnor_2_out, xor_1_out, xor_2_out, xor_3_out, xor_4_out, xor_5_out;
  wire [1:0] and_2_out, and_5_out, ButtonState_2_q, ButtonState_q;
  wire [2:0] and_27_out, MainState_q;

  Button button_1 (.out(button_1_out));
  Button button_2 (.out(button_2_out));
  Button button_3 (.out(button_3_out));
  Clock clock_1 (.out(clock_1_out));
  Register #(.width(2)) ButtonState (.D(and_2_out), .en(1'b1), .Q(ButtonState_q), .clk(clock_1_out));  // open: clr
  Register #(.width(2)) ButtonState_2 (.D(and_5_out), .en(1'b1), .Q(ButtonState_2_q), .clk(clock_1_out));  // open: clr
  xor xor_1 (xor_1_out, ButtonState_q[1], ButtonState_q[0]);
  xor xor_2 (xor_2_out, ButtonState_2_q[1], ButtonState_2_q[0]);
  not not_1 (not_1_out, ButtonState_q[1]);
  and and_1 (and_1_out, not_1_out, ButtonState_q[0]);
  not not_2 (not_2_out, ButtonState_q[1]);
  and and_2 (and_2_out[0], button_1_out, not_2_out, not_3_out);
  not not_3 (not_3_out, ButtonState_q[0]);
  and and_3 (and_2_out[1], button_1_out, xor_1_out);
  not not_4 (not_4_out, ButtonState_2_q[1]);
  and and_4 (and_4_out, not_4_out, ButtonState_2_q[0]);
  and and_5 (and_5_out[0], button_2_out, not_5_out, not_6_out);
  not not_5 (not_5_out, ButtonState_2_q[1]);
  not not_6 (not_6_out, ButtonState_2_q[0]);
  and and_6 (and_5_out[1], button_2_out, xor_2_out);
  Register #(.width(3)) MainState (.D(and_27_out), .en(1'b1), .Q(MainState_q), .clk(clock_1_out));  // open: clr
  not not_7 (not_7_out, MainState_q[1]);
  not not_8 (not_8_out, MainState_q[2]);
  not not_9 (not_9_out, MainState_q[1]);
  not not_10 (not_10_out, MainState_q[2]);
  not not_11 (not_11_out, and_4_out);
  not not_12 (not_12_out, and_1_out);
  not not_13 (not_13_out, MainState_q[2]);
  not not_14 (not_14_out, MainState_q[1]);
  not not_15 (not_15_out, MainState_q[0]);
  LED led_1 (.in(and_7_out));
  and and_7 (and_7_out, MainState_q[2], MainState_q[1], not_16_out);
  not not_16 (not_16_out, MainState_q[0]);
  not not_17 (not_17_out, MainState_q[2]);
  xnor xnor_1 (xnor_1_out, and_1_out, and_4_out);
  xor xor_3 (xor_3_out, and_1_out, and_4_out);
  not not_18 (not_18_out, MainState_q[0]);
  not not_19 (not_19_out, and_1_out);
  not not_20 (not_20_out, MainState_q[0]);
  not not_21 (not_21_out, MainState_q[1]);
  xnor xnor_2 (xnor_2_out, and_1_out, and_4_out);
  not not_22 (not_22_out, and_4_out);
  not not_23 (not_23_out, MainState_q[0]);
  not not_24 (not_24_out, MainState_q[1]);
  not not_25 (not_25_out, MainState_q[2]);
  xor xor_4 (xor_4_out, MainState_q[2], MainState_q[0]);
  not not_26 (not_26_out, and_1_out);
  not not_27 (not_27_out, MainState_q[1]);
  or or_1 (or_1_out, not_11_out, and_1_out);
  not not_28 (not_28_out, MainState_q[0]);
  not not_29 (not_29_out, MainState_q[2]);
  not not_30 (not_30_out, and_4_out);
  not not_31 (not_31_out, MainState_q[2]);
  not not_32 (not_32_out, MainState_q[1]);
  not not_33 (not_33_out, and_1_out);
  not not_34 (not_34_out, MainState_q[1]);
  not not_35 (not_35_out, MainState_q[0]);
  LED led_2 (.in(and_8_out));
  and and_8 (and_8_out, MainState_q[2], not_36_out, MainState_q[0]);
  not not_36 (not_36_out, MainState_q[1]);
  and and_9 (and_9_out, MainState_q[0], MainState_q[1], not_17_out);
  and and_10 (and_10_out, xnor_1_out, MainState_q[0], not_7_out, MainState_q[2]);
  and and_11 (and_11_out, xor_3_out, not_18_out, MainState_q[1], not_8_out);
  and and_12 (and_12_out, not_19_out, and_4_out, not_20_out, not_21_out, MainState_q[2]);
  and and_13 (and_13_out, xnor_2_out, MainState_q[0], not_9_out, not_10_out);
  and and_14 (and_14_out, and_1_out, not_22_out, not_23_out, not_24_out, not_25_out);
  and and_15 (and_15_out, xor_4_out, MainState_q[1]);
  and and_16 (and_16_out, not_26_out, and_4_out, MainState_q[2], not_27_out, MainState_q[0]);
  and and_17 (and_17_out, or_1_out, not_28_out, MainState_q[1], not_29_out);
  and and_18 (and_18_out, and_1_out, not_30_out, not_31_out, not_32_out, MainState_q[0]);
  xor xor_5 (xor_5_out, MainState_q[1], MainState_q[0]);
  or or_2 (or_2_out, not_33_out, and_4_out);
  and and_19 (and_19_out, or_2_out, and_20_out);
  and and_20 (and_20_out, not_34_out, not_35_out, MainState_q[2]);
  LED led_3 (.in(and_21_out));
  and and_21 (and_21_out, MainState_q[2], not_38_out, not_39_out);
  not not_37 (not_37_out, MainState_q[2]);
  not not_38 (not_38_out, MainState_q[1]);
  not not_39 (not_39_out, MainState_q[0]);
  and and_22 (and_22_out, MainState_q[2], xor_5_out);
  and and_23 (and_23_out, and_4_out, not_12_out, not_13_out, not_14_out, not_15_out);
  LED led_4 (.in(or_3_out));
  or or_3 (or_3_out, and_25_out, and_24_out);
  and and_24 (and_24_out, MainState_q[2], MainState_q[1], MainState_q[0]);
  and and_25 (and_25_out, not_37_out, not_40_out, not_41_out);
  not not_40 (not_40_out, MainState_q[1]);
  not not_41 (not_41_out, MainState_q[0]);
  not not_42 (not_42_out, button_3_out);
  or or_4 (or_4_out, and_9_out, and_10_out, and_11_out, and_12_out, and_13_out, and_14_out);
  not not_43 (not_43_out, button_3_out);
  or or_5 (or_5_out, and_15_out, and_16_out, and_17_out, and_18_out);
  not not_44 (not_44_out, button_3_out);
  or or_6 (or_6_out, and_22_out, and_19_out, and_23_out);
  LED led_5 (.in(and_26_out));
  and and_26 (and_26_out, not_45_out, not_46_out, MainState_q[0]);
  not not_45 (not_45_out, MainState_q[2]);
  not not_46 (not_46_out, MainState_q[1]);
  and and_27 (and_27_out[0], not_42_out, or_4_out);
  and and_28 (and_27_out[1], not_43_out, or_5_out);
  and and_29 (and_27_out[2], not_44_out, or_6_out);
  LED led_6 (.in(and_30_out));
  and and_30 (and_30_out, not_47_out, MainState_q[1], not_48_out);
  not not_47 (not_47_out, MainState_q[2]);
  not not_48 (not_48_out, MainState_q[0]);
  LED led_7 (.in(and_31_out));
  and and_31 (and_31_out, not_49_out, MainState_q[1], MainState_q[0]);
  not not_49 (not_49_out, MainState_q[2]);

  // Notes on the sheet:
  //   PLAYER 1
  //   PLAYER 2
  //   RESET
  //   Synchronous Clock
  //   S1
  //   S0
  //   S1
  //   S0
  //   S2
  //   S1
  //   S0
  //   Finish : Player2
  //   N1
  //   N2
  //   Centre
  //   N0
  //   Finish : Player1
endmodule
