// Logisim project Controller.circ as structural Verilog: 1 circuit, main circuit main
module main (
  input  alt,
  input  aeq,
  input  agr,
  input  ach,
  input  go,
  input  CLK,
  output [3:0] STATE,
  output la,
  output sa1,
  output sa2,
  output lb,
  output lm,
  output sm1,
  output sm2,
  output sad1,
  output sad2,
  output sch,
  output ldff,
  output lr
);

  wire and_1_out, and_2_out, and_4_out, and_5_out, and_6_out, and_7_out, and_8_out, and_9_out, and_10_out,
       and_11_out, and_12_out, and_13_out, and_14_out, and_15_out, and_16_out, and_17_out, and_18_out,
       and_19_out, and_20_out, and_21_out, and_22_out, and_23_out, and_24_out, and_25_out, and_26_out,
       and_27_out, and_28_out, and_29_out, and_30_out, and_31_out, and_32_out, and_33_out, and_37_out,
       and_38_out, and_44_out, not_1_out, not_2_out, not_3_out, not_4_out, not_5_out, not_6_out, not_7_out,
       not_8_out, or_1_out, or_2_out, or_3_out, or_4_out, or_5_out, or_6_out, or_7_out, or_8_out, or_9_out,
       or_10_out, or_11_out, xor_1_out, xor_2_out, xor_3_out, xor_4_out;
  wire [3:0] or_16_out;

  Register #(.width(4)) u_State (.D(or_16_out), .en(1'b1), .Q(STATE), .clk(CLK));  // open: clr
  not not_1 (not_1_out, STATE[0]);
  not not_2 (not_2_out, STATE[1]);
  not not_3 (not_3_out, STATE[2]);
  not not_4 (not_4_out, STATE[3]);
  not not_5 (not_5_out, alt);
  not not_6 (not_6_out, aeq);
  not not_7 (not_7_out, agr);
  not not_8 (not_8_out, ach);
  and and_1 (and_1_out, not_4_out, STATE[2], STATE[1]);
  and and_2 (and_2_out, not_1_out, not_8_out);
  and and_3 (or_16_out[3], and_1_out, or_1_out);
  or or_1 (or_1_out, and_2_out, STATE[0]);
  and and_4 (and_4_out, not_4_out, not_3_out, STATE[1], STATE[0]);
  or or_2 (or_2_out, alt, agr);
  and and_5 (and_5_out, not_4_out, STATE[2], not_1_out);
  and and_6 (and_6_out, STATE[1], ach);
  and and_7 (and_7_out, not_4_out, not_3_out, not_2_out, STATE[0]);
  and and_8 (and_8_out, alt, not_6_out, not_7_out);
  or or_3 (or_3_out, aeq, agr);
  and and_9 (and_9_out, not_4_out, not_3_out, STATE[1]);
  and and_10 (and_10_out, not_4_out, not_3_out, not_2_out);
  and and_11 (and_11_out, go, not_1_out);
  and and_12 (and_12_out, STATE[0], not_5_out);
  or or_4 (or_4_out, aeq, agr);
  and and_13 (and_13_out, not_4_out, not_1_out);
  xor xor_1 (xor_1_out, STATE[2], STATE[1]);
  and and_14 (and_14_out, or_2_out, not_6_out);
  or or_5 (or_5_out, and_14_out, and_15_out);
  and and_15 (and_15_out, not_5_out, not_7_out, aeq);
  and and_16 (and_16_out, and_5_out, or_6_out);
  or or_6 (or_6_out, not_2_out, and_6_out);
  or or_7 (or_7_out, and_8_out, and_17_out);
  and and_17 (and_17_out, not_5_out, or_3_out);
  and and_18 (and_18_out, STATE[0], not_5_out, aeq, not_7_out);
  and and_19 (and_19_out, not_4_out, STATE[2]);
  and and_20 (and_20_out, not_2_out, STATE[0]);
  or or_8 (or_8_out, and_20_out, and_21_out);
  and and_21 (and_21_out, not_1_out, STATE[1], ach);
  or or_9 (or_9_out, and_11_out, and_22_out);
  and and_22 (and_22_out, and_12_out, or_4_out);
  and and_23 (and_23_out, and_13_out, xor_1_out);
  and and_24 (and_24_out, not_4_out, STATE[2]);
  and and_25 (and_25_out, not_2_out, STATE[0]);
  and and_26 (and_26_out, STATE[1], not_1_out, ach);
  and and_27 (and_27_out, not_4_out, STATE[2], not_2_out, STATE[0]);
  and and_28 (and_28_out, and_4_out, or_5_out);
  and and_29 (and_29_out, and_7_out, or_7_out);
  and and_30 (and_30_out, and_9_out, or_10_out);
  or or_10 (or_10_out, not_1_out, and_18_out);
  and and_31 (and_31_out, and_19_out, or_8_out);
  and and_32 (and_32_out, and_10_out, or_9_out);
  and and_33 (and_33_out, and_24_out, or_11_out);
  or or_11 (or_11_out, and_25_out, and_26_out);
  xor xor_2 (xor_2_out, STATE[1], STATE[0]);
  and and_34 (sa1, not_4_out, STATE[2], not_2_out, STATE[0]);
  and and_35 (sa2, not_4_out, not_3_out, not_1_out, STATE[1]);
  and and_36 (lb, not_4_out, not_3_out, not_2_out, STATE[0]);
  and and_37 (and_37_out, not_4_out, not_2_out, xor_3_out);
  xor xor_3 (xor_3_out, STATE[2], STATE[0]);
  and and_38 (and_38_out, not_4_out, STATE[2], STATE[1], STATE[0]);
  and and_39 (sm1, not_4_out, not_2_out, not_1_out, STATE[2]);
  and and_40 (sm2, not_4_out, STATE[2], STATE[1], STATE[0]);
  and and_41 (sad1, not_4_out, not_2_out, STATE[2], STATE[0]);
  and and_42 (sad2, not_4_out, not_2_out, STATE[2], STATE[0]);
  and and_43 (sch, not_4_out, not_3_out, not_1_out, STATE[1]);
  or or_12 (or_16_out[2], and_28_out, and_16_out);
  and and_44 (and_44_out, not_4_out, not_3_out, xor_2_out);
  or or_13 (lm, and_37_out, and_38_out);
  and and_45 (ldff, not_4_out, not_3_out, xor_4_out);
  xor xor_4 (xor_4_out, STATE[1], STATE[0]);
  and and_46 (lr, not_3_out, not_2_out, not_1_out, STATE[3]);
  or or_14 (or_16_out[1], and_29_out, and_30_out, and_31_out);
  or or_15 (la, and_44_out, and_27_out);
  or or_16 (or_16_out[0], and_32_out, and_23_out, and_33_out);

  // Notes on the sheet:
  //   P0
  //   P1
  //   P2
  //   P3
  //   P0`
  //   P1`
  //   P2`
  //   P3`
  //   alt`
  //   aeq`
  //   agr`
  //   ach`
  //   N3
  //   N2
  //   N1
  //   N0
endmodule
