// Logisim project Datapath.circ as structural Verilog: 1 circuit, main circuit main
module main (
  input  sch,
  input  ldff,
  input  sm1,
  input  sm2,
  input  lm,
  input  lr,
  input  sad1,
  input  sad2,
  input  [15:0] a_i,
  input  sa1,
  input  sa2,
  input  la,
  input  [15:0] b_i,
  input  lb,
  input  CLK,
  output ach,
  output [15:0] Result,
  output agr,
  output aeq,
  output alt
);

  wire multiplexer_5_out;
  wire [15:0] a_q, adder_1_out, b_q, mult_q, multiplexer_1_out, multiplexer_2_out, multiplexer_3_out,
       multiplexer_4_out, multiplexer_6_out, multiplexer_7_out, negator_1_out, negator_2_out;

  Multiplexer #(.width(16), .enable("false")) multiplexer_1 (
    .in0({16{1'b0}}), .in1(adder_1_out), .out(multiplexer_1_out), .sel(sm1));
  Multiplexer #(.width(16), .enable("false")) multiplexer_2 (
    .in0(multiplexer_1_out), .in1(negator_1_out), .out(multiplexer_2_out), .sel(sm2));
  Multiplexer #(.width(16), .enable("false")) multiplexer_3 (
    .in0(a_i), .in1(adder_1_out), .out(multiplexer_3_out), .sel(sa1));
  Multiplexer #(.width(16), .enable("false")) multiplexer_4 (
    .in0(multiplexer_3_out), .in1(negator_2_out), .out(multiplexer_4_out), .sel(sa2));
  Multiplexer #(.enable("false")) multiplexer_5 (.in0(1'b0), .in1(1'b1), .out(multiplexer_5_out), .sel(sch));
  D_Flip_Flop a_check (.clk(CLK), .D(multiplexer_5_out), .Q(ach), .en(ldff));  // open: Qn, preset, reset
  Register #(.width(16)) mult (.D(multiplexer_2_out), .en(lm), .Q(mult_q), .clk(CLK));  // open: clr
  Register #(.width(16)) a (.D(multiplexer_4_out), .en(la), .Q(a_q), .clk(CLK));  // open: clr
  Register #(.width(16)) b (.D(b_i), .en(lb), .Q(b_q), .clk(CLK));  // open: clr
  Negator #(.width(16)) negator_1 (.in(mult_q), .out(negator_1_out));
  Negator #(.width(16)) negator_2 (.in(a_q), .out(negator_2_out));
  Multiplexer #(.width(16), .enable("false")) multiplexer_6 (
    .in0(mult_q), .in1(a_q), .out(multiplexer_6_out), .sel(sad1));
  Multiplexer #(.width(16), .enable("false")) multiplexer_7 (
    .in0(b_q), .in1({16{1'b1}}), .out(multiplexer_7_out), .sel(sad2));
  Adder #(.width(16)) adder_1 (.a(multiplexer_6_out), .b(multiplexer_7_out), .out(adder_1_out));  // open: cin, cout
  Register #(.width(16)) res (.D(mult_q), .en(lr), .Q(Result), .clk(CLK));  // open: clr
  Comparator #(.width(16)) comparator_1 (.a(a_q), .b({16{1'b0}}), .gt(agr), .eq(aeq), .lt(alt));

  // Notes on the sheet:
  //   a_in_negation
endmodule
