// Logisim project Main.circ as structural Verilog: 1 circuit, main circuit main
module main (
  input  [15:0] Number__A,
  input  [15:0] Number__B,
  output [15:0] Result,
  output [3:0] Current_STATE
);

  wire BUTTON_out, CLK_out, main_1_la, main_1_lb, main_1_ldff, main_1_lm, main_1_lr, main_1_sa1, main_1_sa2,
       main_1_sad1, main_1_sad2, main_1_sch, main_1_sm1, main_1_sm2, main_2_ach, main_2_aeq, main_2_agr,
       main_2_alt;

  Clock CLK (.out(CLK_out));
  Button BUTTON (.out(BUTTON_out));
  Controller_main main_1 (
    .alt(main_2_alt), .aeq(main_2_aeq), .agr(main_2_agr), .ach(main_2_ach), .go(BUTTON_out), .CLK(CLK_out),
    .STATE(Current_STATE), .la(main_1_la), .sa1(main_1_sa1), .sa2(main_1_sa2), .lb(main_1_lb),
    .lm(main_1_lm), .sm1(main_1_sm1), .sm2(main_1_sm2), .sad1(main_1_sad1), .sad2(main_1_sad2),
    .sch(main_1_sch), .ldff(main_1_ldff), .lr(main_1_lr));
  Datapath_main main_2 (
    .sch(main_1_sch), .ldff(main_1_ldff), .sm1(main_1_sm1), .sm2(main_1_sm2), .lm(main_1_lm), .lr(main_1_lr),
    .a_i(Number__A), .sa1(main_1_sa1), .sa2(main_1_sa2), .la(main_1_la), .b_i(Number__B), .lb(main_1_lb),
    .CLK(CLK_out), .sad1(main_1_sad1), .sad2(main_1_sad2), .ach(main_2_ach), .Result(Result),
    .agr(main_2_agr), .aeq(main_2_aeq), .alt(main_2_alt));

  // Notes on the sheet:
  //   Controller
  //   Note : Number 'A' cannot be negative.
  //   Datapath
  //   How To : After numbers are loaded ,  press 'BUTTON' for result of multiplication.
endmodule
